// Logisim project proj.circ as structural Verilog: 3 circuits, main circuit main
module main (
);

  wire and_1_out, and_2_out, and_3_out, and_4_out, and_5_out, and_6_out, and_7_out, clk, comparator_1_eq,
       comparator_2_eq, comparator_3_eq, comparator_4_eq, comparator_5_eq, comparator_5_gt, d_ff_1_q,
       d_ff_2_q, debugger_1_p1, irq, kb_clear, kb_sel, mem, not_1_out, or_1_out, r_w, ram_sel, tim_reset,
       tim_sel, tty_clear, tty_sel, word;
  wire [5:0] int_v;
  wire [6:0] kb_char;
  wire [7:0] kb_control, tty_char, tty_control;
  wire [15:0] addr, counter_1_q, data, debugger_1_p4, debugger_1_p5, fp, pc, ps, r0, r1, r2, r3, r4, r5, r6,
       sp;

  // Probe on r0
  // Probe on fp
  // Probe on r1
  // Probe on r2
  // Probe on sp
  // Probe on pc
  interrupt_manager interrupt_manager_1 (
    .kb_interrupt(kb_control[1]), .tim_interrupt(tim_reset), .int_v(int_v), .IRQ(irq));
  Clock clock_1 (.out(clk));
  // Probe on r3
  // Probe on r4
  // Probe on ps
  // CdM_16 cdm_16_1: pin names not known; wires that end beside it: irq, int_v, r0, r1, r2, r3, r4, r5, r6, fp, pc, sp, ps, mem, r_w, word, addr
  // Debugger debugger_1: pin names not known; wires that end beside it: debugger_1_p1, 1'b0, clk, debugger_1_p4, debugger_1_p5
  // Probe on r6
  // Probe on r5
  not not_1 (not_1_out, r_w);
  assign debugger_1_p5 = r_w ? data : 16'bz;  // Controlled_Buffer controlled_buffer_1
  // Probe on addr
  // Probe on data
  // Probe on data
  assign data = not_1_out ? debugger_1_p4 : 16'bz;  // Controlled_Buffer controlled_buffer_2
  Comparator #(.width(4), .mode("unsigned")) comparator_1 (
    .a(addr[3:0]), .b(4'b0000), .eq(comparator_1_eq));  // open: gt, lt
  Comparator #(.width(4), .mode("unsigned")) comparator_2 (
    .a(addr[3:0]), .b(4'b0010), .eq(comparator_2_eq));  // open: gt, lt
  Keyboard keyboard_1 (.clk(clk), .re(kb_control[0]), .clr(kb_clear), .avail(kb_control[1]), .data(kb_char));
  Pull_Resistor pull_resistor_1 (.node(kb_control[0]));
  Pull_Resistor pull_resistor_2 (.node(kb_clear));
  assign data[7:0] = and_1_out ? {1'b0, kb_char} : 8'bz;  // Controlled_Buffer controlled_buffer_3
  Pull_Resistor pull_resistor_3 (.node(data[15:8]));
  and and_1 (and_1_out, comparator_1_eq, kb_sel);
  assign data[7:0] = and_3_out ? {{5{kb_control[7]}}, kb_clear, kb_control[1:0]} : 8'bz;  // Controlled_Buffer controlled_buffer_4
  Pull_Resistor pull_resistor_4 (.node(data[15:8]));
  assign {{5{kb_control[7]}}, kb_clear, kb_control[1:0]} = and_2_out ? data[7:0] : 8'bz;  // Controlled_Buffer controlled_buffer_5
  and and_2 (and_2_out, comparator_2_eq, ~r_w, kb_sel);  // AND_Gate
  and and_3 (and_3_out, comparator_2_eq, r_w, kb_sel);
  \interconnect  interconnect_1 (.addr(addr), .ram(ram_sel), .kb(kb_sel), .tim(tim_sel), .tty(tty_sel));
  Pull_Resistor pull_resistor_5 (.node(tty_char));
  and and_4 (and_4_out, mem, ram_sel);
  TTY tty_1 (.data(tty_char[6:0]), .clk(clk), .we(d_ff_1_q), .clr(tty_clear));
  D_Flip_Flop d_ff_1 (.clk(clk), .D(tty_control[0]), .Q(d_ff_1_q));  // open: Qn, preset, en, reset
  Pull_Resistor pull_resistor_6 (.node(tty_clear));
  // RAM ram_1: pin names not known; wires that end beside it: debugger_1_p1, addr, word, and_4_out, clk, r_w, data
  Counter #(.width(16), .max('hffff)) counter_1 (
    .Q(counter_1_q), .clk(clk), .clr(d_ff_2_q));  // open: load, D, count, carry
  D_Flip_Flop d_ff_2 (.clk(clk), .D(tim_reset), .Q(d_ff_2_q));  // open: Qn, preset, en, reset
  Comparator #(.width(4), .mode("unsigned")) comparator_3 (
    .a(addr[3:0]), .b(4'b1000), .eq(comparator_3_eq));  // open: gt, lt
  Comparator #(.width(4), .mode("unsigned")) comparator_4 (
    .a(addr[3:0]), .b(4'b1010), .eq(comparator_4_eq));  // open: gt, lt
  Comparator #(.width(16)) comparator_5 (
    .a(counter_1_q), .b(16'h64), .gt(comparator_5_gt), .eq(comparator_5_eq));  // open: lt
  or or_1 (or_1_out, comparator_5_gt, comparator_5_eq);
  assign tty_char = and_5_out ? data[7:0] : 8'bz;  // Controlled_Buffer controlled_buffer_6
  and and_5 (and_5_out, comparator_3_eq, tty_sel);
  Pull_Resistor pull_resistor_7 (.node(data[15:8]));
  assign data[7:0] = and_6_out ? {{6{tty_control[7]}}, tty_clear, tty_control[0]} : 8'bz;  // Controlled_Buffer controlled_buffer_7
  Pull_Resistor pull_resistor_8 (.node(data[15:8]));
  assign {{6{tty_control[7]}}, tty_clear, tty_control[0]} = and_7_out ? data[7:0] : 8'bz;  // Controlled_Buffer controlled_buffer_8
  and and_6 (and_6_out, comparator_4_eq, r_w, tty_sel);
  and and_7 (and_7_out, comparator_4_eq, ~r_w, tty_sel);  // AND_Gate
  D_Flip_Flop d_ff_3 (.clk(clk), .D(or_1_out), .Q(tim_reset));  // open: Qn, preset, en, reset
  // also tied to GND on the sheet: {kb_control[7], tty_control[7]}

  // Other names for the same wires on the sheet: kb_next = kb_control[0]; kb_ready = kb_control[1];
  //   kb_control[6:2] = {{4{kb_control[7]}}, kb_clear}; tty_enable = tty_control[0];
  //   tty_control[6:1] = {{5{tty_control[7]}}, tty_clear}

  // Notes on the sheet:
  //   Процессор
  //   Регистр состояния
  //   Подай следующий!
  //   Очисти!
  //   Отображение на память ;( Я мне кажется переусложнил немнога
  //   read/write регистр
  //   Устройства
  //   Клавиатура
  //   Писать сюда :D
  //   Есть символ?
  //   Регистр Символа
  //   Таймер
  //   read/write регистр
  //   Память
  //   Терминал
  //   Отображение на память ;(
endmodule

module \interconnect  (
  input  [15:0] addr,
  output ram,
  output kb,
  output tty,
  output tim
);

  wire comparator_2_lt, comparator_3_lt, comparator_4_lt;

  Comparator #(.width(16), .mode("unsigned")) comparator_1 (.a(addr), .b(16'hf000), .lt(ram));  // open: gt, eq
  Comparator #(.width(16), .mode("unsigned")) comparator_2 (
    .a(addr), .b(16'hf008), .lt(comparator_2_lt));  // open: gt, eq
  Comparator #(.width(16), .mode("unsigned")) comparator_3 (
    .a(addr), .b(16'hf00f), .lt(comparator_3_lt));  // open: gt, eq
  Comparator #(.width(16), .mode("unsigned")) comparator_4 (
    .a(addr), .b(16'hf018), .lt(comparator_4_lt));  // open: gt, eq
  and and_1 (kb, ~ram, comparator_2_lt);  // AND_Gate
  and and_2 (tty, ~comparator_2_lt, comparator_3_lt);  // AND_Gate
  and and_3 (tim, ~comparator_3_lt, comparator_4_lt);  // AND_Gate
endmodule

module interrupt_manager (
  input  kb_interrupt,
  input  tim_interrupt,
  output [5:0] int_v,
  output IRQ
);

  Multiplexer #(.select(2), .width(6)) multiplexer_1 (
    .in0(6'b000110), .in1(6'b000110), .in2(6'b000101), .in3(6'b000110), .out(int_v),
    .sel({kb_interrupt, tim_interrupt}));  // open: en
  or or_1 (IRQ, kb_interrupt, tim_interrupt);
endmodule
