// Logisim project test.circ as structural Verilog: 1 circuit, main circuit main
module main (
);

  wire cdm_16e_1_p1, clk, not_1_out, r_w;
  wire [15:0] addr, cdm_16e_1_p5, cdm_16e_1_p6, data;

  Clock clock_1 (.out(clk));
  // Probe on cdm_16e_1_p1
  // CdM_16e cdm_16e_1: pin names not known; wires that end beside it: cdm_16e_1_p1, clk, r_w, addr, cdm_16e_1_p5, cdm_16e_1_p6
  not not_1 (not_1_out, r_w);
  assign cdm_16e_1_p6 = r_w ? data : 16'bz;  // Controlled_Buffer controlled_buffer_1
  assign data = not_1_out ? cdm_16e_1_p5 : 16'bz;  // Controlled_Buffer controlled_buffer_2
  // NOT_Gate not_2 has open pins: in=r_w, out=open
  // RAM ram_1: pin names not known; wires that end beside it: addr, clk, r_w, data
endmodule
